# Fritzing sketch beerStock (saved by Fritzing 0.9.2b)
breadboards: 1

parts:
  R1 = Resistor [tolerance=±5% resistance=2.2k package=THT]
  Raspberry_Pi_B_rev1 = Raspberry Pi B rev1
  Q1 = NPN-Transistor [package="TO92 [THT]"]
  Power_plug1 = Power plug
  R2 = Resistor [tolerance=±5% resistance=10k package=THT]
  S1 = Toggle Switch [package=THT]
  U2 = 2-Channel 5v Relay Shield [package=relay-2ch5v10a]
  U3 = ID-12_20 [part_number=RFID package=id-12]
  U4 = HALL-EFFECT [package=sc70]
  VALVE1 = Plastic Solenoid Valve

nets:
  N1: R1.Pin_0, Raspberry_Pi_B_rev1.GPIO_7, R2.Pin_1
  N2: R1.Pin_1, Q1.C
  N3: Raspberry_Pi_B_rev1.3V3, Raspberry_Pi_B_rev1.GPIO_0, U3.FUTURE
  VCC: Raspberry_Pi_B_rev1.5V, U2.VCC, U4.VCC
  N4: Raspberry_Pi_B_rev1.GPIO_23, Raspberry_Pi_B_rev1.GPIO_24, U4.OUT
  N5: Raspberry_Pi_B_rev1.GPIO_10, Raspberry_Pi_B_rev1.GPIO_9, U3.ANT1
  N6: Raspberry_Pi_B_rev1.GPIO_25, U3.CP
  GND: Raspberry_Pi_B_rev1.GPIO_11, Raspberry_Pi_B_rev1.GND, Q1.B, R2.Pin_0, U2.JD-GND, U3.RES, U3.ANT2, U4.GND
  N7: Raspberry_Pi_B_rev1.GPIO_8, U3.GNDT
  N8: Q1.E, S1.COM
  N9: Power_plug1.GND, VALVE1.no_name_yet#2
  N10: Power_plug1.VCC, U2.K1-On
  N11: S1.L2, U2.IN1
  N12: U2.K1-In, VALVE1.no_name_yet#1

notes:
  débitmètre
  RFID
  électrovanne
  alimenation 12V max

custom parts:
  2-Channel 5v Relay Shield: 2 Channel 5v Relay Shield w. 2x SPD-06VDC-SD-C
